// Logisim project final functional.circ as structural Verilog: 2 circuits, main circuit main
module main (
  input  in_1,
  input  I_lsb,
  input  I_msb,
  input  in_4,
  input  clock,
  input  reset,
  output O_msb,
  output out_8,
  output out_9,
  output O_lsb
);

  wire decoder_1_out10, decoder_1_out11, decoder_1_out12, decoder_1_out13, decoder_1_out14, decoder_1_out15,
       decoder_2_out1, decoder_2_out2, decoder_2_out3, decoder_2_out4, decoder_2_out5, decoder_2_out6,
       decoder_2_out7, decoder_2_out8, decoder_2_out9, decoder_2_out10, or_1_out, or_2_out, or_3_out,
       or_4_out, or_5_out;
  wire [3:0] multiplexer_1_out;

  Decoder #(.select(4)) decoder_1 (
    .out10(decoder_1_out10), .out11(decoder_1_out11), .out12(decoder_1_out12), .out13(decoder_1_out13),
    .out14(decoder_1_out14), .out15(decoder_1_out15), .sel({O_msb, out_8, out_9, O_lsb}));  // open: out0, out1, out2, out3, out4, out5, out6, out7, out8, out9, en
  Multiplexer #(.width(4), .disabled(0), .enable("false")) multiplexer_1 (
    .in0({I_msb, in_4, in_1, I_lsb}), .in1({I_msb, in_4, in_1, I_lsb}), .out(multiplexer_1_out),
    .sel(or_1_out));
  or or_1 (or_1_out, decoder_1_out10, decoder_1_out11, decoder_1_out12, decoder_1_out13, decoder_1_out14, decoder_1_out15);
  Pull_Resistor pull_resistor_1 (.node(I_msb));
  Pull_Resistor pull_resistor_2 (.node(in_4));
  Decoder #(.select(4)) decoder_2 (
    .out1(decoder_2_out1), .out2(decoder_2_out2), .out3(decoder_2_out3), .out4(decoder_2_out4),
    .out5(decoder_2_out5), .out6(decoder_2_out6), .out7(decoder_2_out7), .out8(decoder_2_out8),
    .out9(decoder_2_out9), .out10(decoder_2_out10), .out11(decoder_2_out10), .out12(decoder_2_out10),
    .out13(decoder_2_out10), .out14(decoder_2_out10), .out15(decoder_2_out10), .sel(multiplexer_1_out));  // open: out0, en
  or or_2 (or_2_out, decoder_2_out9, decoder_2_out8, decoder_2_out7, decoder_2_out6, decoder_2_out5);
  D_Flip_Flop d_ff_1 (.clk(clock), .D(or_2_out), .Q(O_msb), .reset(reset));  // open: Qn, preset, en
  Pull_Resistor pull_resistor_3 (.node(in_1));
  or or_3 (or_3_out, decoder_2_out4, decoder_2_out9);
  D_Flip_Flop d_ff_2 (.clk(clock), .D(or_3_out), .Q(out_8), .reset(reset));  // open: Qn, preset, en
  or or_4 (or_4_out, decoder_2_out8, decoder_2_out7, decoder_2_out3, decoder_2_out2);
  D_Flip_Flop d_ff_3 (.clk(clock), .D(or_4_out), .Q(out_9), .reset(reset));  // open: Qn, preset, en
  or or_5 (or_5_out, decoder_2_out8, decoder_2_out6, decoder_2_out3, decoder_2_out1);
  D_Flip_Flop d_ff_4 (.clk(clock), .D(or_5_out), .Q(O_lsb), .reset(reset));  // open: Qn, preset, en
endmodule

module serialbcd (
  input  in_1,
  input  in_2,
  input  in_3,
  input  in_4,
  input  in_5,
  input  in_6,
  input  in_7,
  input  in_8,
  input  in_9,
  input  in_10,
  input  in_11,
  input  in_12,
  input  in_13,
  input  in_14,
  input  reset,
  input  in_16,
  input  in_17
);

  wire and_1_out, clock_1_out, counter_1_carry, main_3_o_lsb, main_3_out_8, main_3_out_9, main_4_o_lsb,
       main_4_out_8, main_4_out_9, main_5_o_lsb, main_5_out_8, main_5_out_9, multiplexer_1_out, n7448_1_p1,
       n7448_1_p2, n7448_1_p6, n7448_1_p7, n7448_1_p8, n7448_1_p9, n7448_1_p10, n7448_1_p11, n7448_1_p12,
       n7448_1_p13, n7448_1_p14, n7448_2_p1, n7448_2_p2, n7448_2_p6, n7448_2_p7, n7448_2_p8, n7448_2_p9,
       n7448_2_p10, n7448_2_p11, n7448_2_p12, n7448_2_p13, n7448_2_p14, n7448_3_p7, n7448_3_p8, n7448_3_p9,
       n7448_3_p10, n7448_3_p11, n7448_3_p12, n7448_3_p13, n7448_3_p14, n7448_4_p7, n7448_4_p8, n7448_4_p9,
       n7448_4_p10, n7448_4_p11, n7448_4_p12, n7448_4_p13, n7448_4_p14, n7448_5_p8, n7448_5_p9, n7448_5_p10,
       n7448_5_p11, n7448_5_p12, n7448_5_p13, n7448_5_p14;
  wire [3:0] counter_1_q;

  _7_Segment_Display u_7_segment_display_1 (
    .g(n7448_1_p9), .f(n7448_1_p8), .a(n7448_1_p10), .b(n7448_1_p11), .e(n7448_1_p14), .d(n7448_1_p13),
    .c(n7448_1_p12));  // open: dp
  // _7448 7448_1: pin names not known; wires that end beside it: n7448_1_p1, n7448_1_p2, 1'b1, 1'b0, 1'b0, n7448_1_p6, n7448_1_p7, n7448_1_p8, n7448_1_p9, n7448_1_p10, n7448_1_p11, n7448_1_p12, n7448_1_p13, n7448_1_p14
  main main_1 (
    .I_msb(n7448_1_p6), .in_4(n7448_1_p2), .in_1(n7448_1_p1), .I_lsb(n7448_1_p7), .out_8(n7448_1_p6),
    .out_9(n7448_1_p2), .O_lsb(n7448_1_p1), .clock(and_1_out), .reset(reset));  // open: O_msb
  _7_Segment_Display u_7_segment_display_2 (
    .g(n7448_2_p9), .f(n7448_2_p8), .a(n7448_2_p10), .b(n7448_2_p11), .e(n7448_2_p14), .d(n7448_2_p13),
    .c(n7448_2_p12));  // open: dp
  // _7448 7448_2: pin names not known; wires that end beside it: n7448_2_p1, n7448_2_p2, 1'b1, 1'b0, 1'b0, n7448_2_p6, n7448_2_p7, n7448_2_p8, n7448_2_p9, n7448_2_p10, n7448_2_p11, n7448_2_p12, n7448_2_p13, n7448_2_p14
  main main_2 (
    .I_msb(n7448_2_p6), .in_4(n7448_2_p2), .in_1(n7448_2_p1), .I_lsb(n7448_2_p7), .O_msb(n7448_1_p7),
    .out_8(n7448_2_p6), .out_9(n7448_2_p2), .O_lsb(n7448_2_p1), .clock(and_1_out), .reset(reset));
  main main_3 (
    .I_msb(main_3_out_8), .in_4(main_3_out_9), .in_1(main_3_o_lsb), .I_lsb(n7448_3_p7), .O_msb(n7448_2_p7),
    .out_8(main_3_out_8), .out_9(main_3_out_9), .O_lsb(main_3_o_lsb), .clock(and_1_out), .reset(reset));
  Multiplexer #(.select(4)) multiplexer_1 (
    .in0(in_1), .in1(in_2), .in2(in_3), .in3(in_4), .in4(in_5), .in5(in_6), .in6(in_7), .in7(in_8),
    .in8(in_9), .in9(in_10), .in10(in_11), .in11(in_12), .in12(in_13), .in13(in_14), .in14(in_16),
    .in15(in_17), .out(multiplexer_1_out), .sel(counter_1_q), .en(1'b1));
  _7_Segment_Display u_7_segment_display_3 (
    .g(n7448_3_p9), .f(n7448_3_p8), .a(n7448_3_p10), .b(n7448_3_p11), .e(n7448_3_p14), .d(n7448_3_p13),
    .c(n7448_3_p12));  // open: dp
  // _7448 7448_3: pin names not known; wires that end beside it: main_3_o_lsb, main_3_out_9, 1'b1, 1'b0, 1'b0, main_3_out_8, n7448_3_p7, n7448_3_p8, n7448_3_p9, n7448_3_p10, n7448_3_p11, n7448_3_p12, n7448_3_p13, n7448_3_p14
  Clock clock_1 (.out(clock_1_out));
  and and_1 (and_1_out, clock_1_out, ~counter_1_carry);  // AND_Gate
  Counter #(.width(4), .max('hf)) counter_1 (
    .count(1'b1), .Q(counter_1_q), .carry(counter_1_carry), .clk(and_1_out), .clr(reset));  // open: load, D
  main main_4 (
    .I_msb(main_4_out_8), .in_4(main_4_out_9), .in_1(main_4_o_lsb), .I_lsb(n7448_4_p7), .O_msb(n7448_3_p7),
    .out_8(main_4_out_8), .out_9(main_4_out_9), .O_lsb(main_4_o_lsb), .clock(and_1_out), .reset(reset));
  _7_Segment_Display u_7_segment_display_4 (
    .g(n7448_4_p9), .f(n7448_4_p8), .a(n7448_4_p10), .b(n7448_4_p11), .e(n7448_4_p14), .d(n7448_4_p13),
    .c(n7448_4_p12));  // open: dp
  // _7448 7448_4: pin names not known; wires that end beside it: main_4_o_lsb, main_4_out_9, 1'b1, 1'b0, 1'b0, main_4_out_8, n7448_4_p7, n7448_4_p8, n7448_4_p9, n7448_4_p10, n7448_4_p11, n7448_4_p12, n7448_4_p13, n7448_4_p14
  main main_5 (
    .I_msb(main_5_out_8), .in_4(main_5_out_9), .in_1(main_5_o_lsb), .I_lsb(multiplexer_1_out),
    .O_msb(n7448_4_p7), .out_8(main_5_out_8), .out_9(main_5_out_9), .O_lsb(main_5_o_lsb), .clock(and_1_out),
    .reset(reset));
  _7_Segment_Display u_7_segment_display_5 (
    .g(n7448_5_p9), .f(n7448_5_p8), .a(n7448_5_p10), .b(n7448_5_p11), .e(n7448_5_p14), .d(n7448_5_p13),
    .c(n7448_5_p12));  // open: dp
  // _7448 7448_5: pin names not known; wires that end beside it: main_5_o_lsb, main_5_out_9, 1'b1, 1'b0, 1'b0, main_5_out_8, multiplexer_1_out, n7448_5_p8, n7448_5_p9, n7448_5_p10, n7448_5_p11, n7448_5_p12, n7448_5_p13, n7448_5_p14
endmodule
